# Fritzing sketch OpenVRT (saved by Fritzing 0.9.3b)
breadboards: 1

parts:
  Part1 = Arduino Mega 2560 (Rev3)
  Part2 = Arduino Motor Shield (Rev3)
  M1 = DC Motor
  Part3 = Bluetooth HC-05 Macho
  U1 = POT [package=pot_alpha_rv16af-20]
  R1 = Resistor [tolerance=±5% resistance=220 package="2512 [SMD]"]
  R2 = Resistor [tolerance=±5% resistance=470 package="2512 [SMD]"]
  R3 = Resistor [tolerance=±5% resistance=1k package=THT]
  M2 = fc-51 [package=THT]
  J1 = ATX24 Pin Power Supply Connector [package=atx24_right_angle]
  D1 = LTE-302 [package=lte-302]  # not connected
  R4 = Resistor [tolerance=±5% resistance=6.8k package="2512 [SMD]"]
  R5 = Resistor [tolerance=±5% resistance=220 package="2512 [SMD]"]
  S1 = Square Pushbutton  # not connected

nets:
  N1: Part1.A8, U1.S
  N2: Part1.D21/SCL, R4.Pin_0, R5.Pin_0
  N3: Part1.D19/RX1, Part3.TXD
  N4: Part1.D18/TX1, R2.Pin_1
  5V: Part1.5V, Part3.VCC, U1.E, R1.Pin_0
  GND: Part1.GND, Part3.GND, U1.A, R3.Pin_1
  N5: Part2.B-, M1.pin_2
  N6: Part2.B+, M1.pin_1
  N7: Part2.VMOT, M2.pin3, J1.12V
  GND_2: Part2.GND, J1.GND
  N8: Part3.RXD, R2.Pin_0, R3.Pin_0
  N9: M2.pin1, R4.Pin_1

notes:
  LJ12A3-4-Z/BY
  12V
